# Fritzing sketch Arduino and motor driver Sketch (saved by Fritzing 0.9.10b)
breadboards: 1

parts:
  L298N1 = L298N DC motor driver
  Part1 = Arduino Uno (Rev3)  # not connected
  Part2 = Arduino Ethernet Shield (Rev3)
  M1 = fc-51 [package=THT]
  M2 = fc-51 [package=THT]
  M3 = fc-51 [package=THT]
  M4 = fc-51 [package=THT]

nets:
  N1: L298N1.5V, L298N1.ENA, Part2.PWM_D3
  N2: L298N1.ENB, Part2.PWM_D11
  N3: L298N1.IN1, Part2.D2
  N4: L298N1.IN2, Part2.SPI/D13
  N5: L298N1.IN3, Part2.D7
  N6: L298N1.IN4, Part2.D8
  N7: Part2.A0, M2.pin1
  N8: Part2.A1, M1.pin1
  N9: Part2.A2, M4.pin1
  N10: Part2.A3, M3.pin1
  N11: Part2.5V, M1.pin3, M2.pin3, M3.pin3, M4.pin3
  N12: Part2.GND, M1.pin2, M2.pin2, M3.pin2, M4.pin2

notes:
  Railway Track 1
  Railway Track 2
  12v power supply
  The ethernet shield is placed on top of the arduino

custom parts:
  L298N DC motor driver: 2x DC motor driver with 78M05 positive voltage regulator (7..35 V) L298N: max 46 V, 2 A Set 5 V Enable jumper to enable 5 V regultor (needed for the L298N) and +5 V output at screw terminal or supply external +5 V at screw terminal Set ENA and/or ENB to +5 V to enable motor permanently or supply ENA and/or ENB with PWM signal IN1 and IN2 set rotation directory for motor A (OUT1/OUT2) IN2 and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
