# Fritzing sketch PLC Sketch (saved by Fritzing 0.9.10b)
breadboards: 1

parts:
  LED4 = LED - 5mm [color="Green (555nm)" current=0.030 package="5 mm [THT]"]
  VCC2 = 4 x AAA Battery Mount
  R1 = Resistor [tolerance=±5% power=0.25 resistance=220 package=THT]
  R2 = Resistor [tolerance=±5% power=0.25 resistance=220 package=THT]
  R3 = Resistor [tolerance=±5% power=0.25 resistance=220 package=THT]
  LED13 = LED - 5mm [color="Yellow (585nm)" current=0.030 package="5 mm [THT]"]
  LED14 = LED - 5mm [color="Red (635nm)" current=0.030 package="5 mm [THT]"]
  R4 = Resistor [tolerance=±5% power=0.25 resistance=220 package=THT]
  LED15 = LED - 5mm [color="Red (635nm)" current=0.030 package="5 mm [THT]"]
  R5 = Resistor [tolerance=±5% power=0.25 resistance=220 package=THT]
  R6 = Resistor [tolerance=±5% power=0.25 resistance=220 package=THT]
  LED16 = LED - 5mm [color="Yellow (595nm)" current=0.030 package="5 mm [THT]"]
  LED17 = LED - 5mm [color="Green (555nm)" current=0.030 package="5 mm [THT]"]
  VCC1 = 4 x AAA Battery Mount

nets:
  N1: LED4.cathode, R1.Pin_1
  N2: VCC2.-, R1.Pin_0, R2.Pin_0, R3.Pin_0
  N3: R2.Pin_1, LED13.cathode
  N4: R3.Pin_1, LED14.cathode
  N5: R4.Pin_0, LED15.cathode
  N6: R4.Pin_1, R5.Pin_1, R6.Pin_1, VCC1.-
  N7: R5.Pin_0, LED16.cathode
  N8: R6.Pin_0, LED17.cathode
